# Fritzing sketch Tank126P Joystick (saved by Fritzing 1.0.3b)
breadboards: 1

parts:
  Part1 = Arduino Nano (Rev3.0)
  Left = KY-023 Dual Axis Joystick Module [package="Breakout board"]
  Right = KY-023 Dual Axis Joystick Module [package="Breakout board"]
  Lights = Toggle Switch [package=THT]
  Headlights = Toggle Switch [package=THT]
  S3 = Pushbutton [package="[THT]"]
  S4 = Pushbutton [package="[THT]"]
  Blinkers = Toggle Switch [package=THT]
  U1 = RF-LINK_TX [package=rf-link_tx]

nets:
  GND: Part1.GND, Left.GND, Right.GND, Lights.COM, Headlights.COM, S3.Pin_3, S3.Pin_4, S4.Pin_3, S4.Pin_4, Blinkers.COM, U1.GND
  N1: Part1.D3, Headlights.L1
  N2: Part1.D4, Lights.L1
  N3: Part1.D5, Blinkers.L1
  N4: Part1.D6, Blinkers.L2
  N5: Part1.D7, U1.DATA
  N6: Part1.D8, S4.Pin_1, S4.Pin_2
  N7: Part1.D9, Left.SW
  N8: Part1.D10, Right.SW
  N9: Part1.D11/MOSI, S3.Pin_1, S3.Pin_2
  +5V: Part1.5V, Left.+5V, Right.+5V, U1.+5V
  N10: Part1.A3, Right.VRy
  N11: Part1.A2, Right.VRx
  N12: Part1.A1, Left.VRy
  N13: Part1.A0, Left.VRx

custom parts:
  KY-023 Dual Axis Joystick Module: KY-023 Dual-Axis Joystick Module.
