# Fritzing sketch Tank126P receiver (saved by Fritzing 1.0.3b)
breadboards: 1

parts:
  U1 = NodeMCU V1.0
  U2 = RF-LINK_RX [package=rf-link_rx]
  R1 = Resistor [tolerance=±5% power=0.25W resistance=220 package=THT]
  R2 = Resistor [tolerance=±5% power=0.25W resistance=220 package=THT]
  LED1 = LED - 5mm [color="Red (633nm)" current=30mA package="5 mm [THT]"]
  LED2 = LED - 5mm [color="Red (633nm)" current=0.030A package="5 mm [THT]"]
  LED6 = LED - 5mm [color="White (4500K)" current=30mA package="5 mm [THT]"]
  LED10 = LED - 5mm [color="White (4500K)" current=30mA package="5 mm [THT]"]
  R3 = Resistor [tolerance=±5% power=0.25W resistance=220 package=THT]
  R4 = Resistor [tolerance=±5% power=0.25W resistance=220 package=THT]
  R5 = Resistor [tolerance=±5% power=0.25W resistance=220 package=THT]
  R6 = Resistor [tolerance=±5% power=0.25W resistance=220 package=THT]
  R7 = Resistor [tolerance=±5% power=0.25W resistance=220 package=THT]
  R8 = Resistor [tolerance=±5% power=0.25W resistance=220 package=THT]
  R9 = Resistor [tolerance=±5% power=0.25W resistance=220 package=THT]
  R10 = Resistor [tolerance=±5% power=0.25W resistance=220 package=THT]
  LED4 = LED - 3mm [color="Yellow (595nm)" current=30mA package="3 mm [THT]"]
  LED5 = LED - 3mm [color="Yellow (595nm)" current=30mA package="3 mm [THT]"]
  LED3 = LED - 3mm [color="Yellow (595nm)" current=30mA package="3 mm [THT]"]
  LED7 = LED - 3mm [color="Yellow (595nm)" current=30mA package="3 mm [THT]"]
  LED8 = LED - 3mm [color="Yellow (595nm)" current=30mA package="3 mm [THT]"]
  LED9 = LED - 3mm [color="Yellow (595nm)" current=30mA package="3 mm [THT]"]

nets:
  N1: U1.D0, U2.DATA
  N2: U1.D1, LED1.anode, LED2.anode
  N3: U1.D2, LED6.anode, LED10.anode
  GND: U1.GND, U2.GND, R1.Pin_0, R2.Pin_1, R3.Pin_0, R5.Pin_0, R6.Pin_0, R7.Pin_1, R9.Pin_1, R10.Pin_1
  N4: U1.D5, LED7.anode, LED8.anode, LED9.anode
  N5: U1.D6, LED4.anode, LED5.anode, LED3.anode
  VIN: U1.Vin, U2.+5V
  N6: R1.Pin_1, LED1.cathode
  N7: R2.Pin_0, LED2.cathode
  N8: LED6.cathode, R6.Pin_1
  N9: LED10.cathode, R10.Pin_0
  N10: R3.Pin_1, LED3.cathode
  N11: R4.Pin_1, LED4.cathode
  N12: R5.Pin_1, LED5.cathode
  N13: R7.Pin_0, LED7.cathode
  N14: R8.Pin_0, LED8.cathode
  N15: R9.Pin_0, LED9.cathode

custom parts:
  NodeMCU V1.0: ESP8266 based NodeMCU
